// Logisim project aaaa.circ as structural Verilog: 1 circuit, main circuit main
module main (
  input  p,
  input  q,
  input  r,
  input  s
);

  wire and_1_out, and_2_out, and_3_out, and_4_out, not_1_out, not_2_out, not_3_out, not_4_out, or_1_out;

  not not_1 (not_1_out, q);
  not not_2 (not_2_out, s);
  not not_3 (not_3_out, p);
  not not_4 (not_4_out, r);
  and and_1 (and_1_out, p, not_1_out, s);
  and and_2 (and_2_out, p, q, not_2_out);
  and and_3 (and_3_out, not_3_out, q, r);
  and and_4 (and_4_out, q, not_4_out, s);
  or or_1 (or_1_out, and_1_out, and_2_out, and_3_out, and_4_out);

  // Notes on the sheet:
  //   -q
  //   -p
  //   q
  //   r
  //   -r
  //   p
  //   s
  //   p
  //   q
  //   -s
  //   q
  //   s
  //   (p.-q.s)
  //   (p.q.-s)
  //   (-p.q.r)
  //   (q.-r.s)
  //   (p.-q.s)+(p.q.-s)+(-p.q.r)+(q.-r.s)
endmodule
